# Fritzing sketch MaltBoard (saved by Fritzing 0.8.7b)
breadboards: 1

parts:
  U1 = atmega328 [package=dip]
  R1 = Resistor [tolerance=±5% resistance=10k package=THT]
  C1 = Electrolytic Capacitor [capacitance=10µF package="100 mil [THT, electrolytic]"]
  XTAL1 = Crystal [frequency="16 Mhz" package=SMD]
  R2 = Resistor [tolerance=±5% resistance=10k package=THT]
  S1 = Pushbutton [package="[THT]"]
  C2 = Ceramic Capacitor [capacitance=22pF package="100 mil [THT, multilayer]"]
  C3 = Ceramic Capacitor [capacitance=22pF package="100 mil [THT, multilayer]"]
  Power_plug2 = Power plug

nets:
  N1: U1.RESET, R2.Pin_0, S1.Pin_1, S1.Pin_2
  VCC: U1.VCC, U1.AVCC, U1.AREF, Power_plug2.VCC
  N2: U1.GND, C1.-, R2.Pin_1, S1.Pin_3, S1.Pin_4, C2.0, C3.1
  N3: U1.XLAT1, XTAL1.pin_1, C3.0
  N4: U1.XLAT2, XTAL1.pin_0, C2.1
  N5: U1.D9_(PWM), R1.Pin_1
  N6: R1.Pin_0, C1.+
